// Logisim project EX.circ as structural Verilog: 13 circuits, main circuit Processor
module main (
  input  isBranchTaken,
  input  [31:0] branchPC,
  input  Reset,
  output [31:0] PC,
  output [31:0] Instruction
);

  wire Clk_out;
  wire [31:0] adder_1_out, multiplexer_1_out;

  Register #(.width(32), .trigger("falling")) u_PC (
    .D(multiplexer_1_out), .en(1'b1), .Q(PC), .clk(Clk_out), .clr(Reset));
  Clock Clk (.out(Clk_out));
  Adder #(.width(32)) adder_1 (.a(32'h4), .b(PC), .out(adder_1_out));  // open: cin, cout
  ROM #(.addrWidth(24), .dataWidth(32)) rom_1 (.addr(PC[25:2]), .data(Instruction));  // open: sel
  Multiplexer #(.width(32), .enable("false")) multiplexer_1 (
    .in0(adder_1_out), .in1(branchPC), .out(multiplexer_1_out), .sel(isBranchTaken));

  // Notes on the sheet:
  //   contents of rom_1 (hex, n*v repeats v):
  //   54400003 54400024
endmodule

// Reg File
module Register_File (
  input  Reset,
  input  Clock,
  input  [31:0] WriteD,
  input  [3:0] Rs1,
  input  WriteE,
  input  [3:0] WriteA,
  input  [3:0] Rs2,
  input  [3:0] Shiftregister,
  output [31:0] D1,
  output [31:0] D2,
  output [4:0] ShiftAmt
);

  wire demultiplexer_1_out0, demultiplexer_1_out1, demultiplexer_1_out2, demultiplexer_1_out3,
       demultiplexer_1_out4, demultiplexer_1_out5, demultiplexer_1_out6, demultiplexer_1_out7,
       demultiplexer_1_out8, demultiplexer_1_out9, demultiplexer_1_out10, demultiplexer_1_out11,
       demultiplexer_1_out12, demultiplexer_1_out13, demultiplexer_1_out14, demultiplexer_1_out15, or_1_out,
       or_2_out;
  wire [31:0] multiplexer_1_out, r0_q, r1_q, r2_q, r3_q, r4_q, r5_q, r6_q, r7_q, r8_q, r9_q, r10_q, r11_q,
       r12_q, r13_q, r14_q, r15_q;
  wire [31:5] multiplexer_4_out;

  Demultiplexer #(.select(4), .disabled(0), .enable("false")) demultiplexer_1 (
    .out0(demultiplexer_1_out0), .out1(demultiplexer_1_out1), .out2(demultiplexer_1_out2),
    .out3(demultiplexer_1_out3), .out4(demultiplexer_1_out4), .out5(demultiplexer_1_out5),
    .out6(demultiplexer_1_out6), .out7(demultiplexer_1_out7), .out8(demultiplexer_1_out8),
    .out9(demultiplexer_1_out9), .out10(demultiplexer_1_out10), .out11(demultiplexer_1_out11),
    .out12(demultiplexer_1_out12), .out13(demultiplexer_1_out13), .out14(demultiplexer_1_out14),
    .out15(demultiplexer_1_out15), .in(WriteE), .sel(WriteA));
  Multiplexer #(.width(32), .enable("false")) multiplexer_1 (
    .in0(WriteD), .in1(32'h3fffffc), .out(multiplexer_1_out), .sel(Reset));
  or or_1 (or_1_out, demultiplexer_1_out14, Reset);
  or or_2 (or_2_out, Clock, Reset);
  Register #(.width(32)) r0 (.D(WriteD), .en(demultiplexer_1_out0), .Q(r0_q), .clk(Clock), .clr(Reset));
  Register #(.width(32)) r1 (.D(WriteD), .en(demultiplexer_1_out1), .Q(r1_q), .clk(Clock), .clr(Reset));
  Register #(.width(32)) r2 (.D(WriteD), .en(demultiplexer_1_out2), .Q(r2_q), .clk(Clock), .clr(Reset));
  Register #(.width(32)) r3 (.D(WriteD), .en(demultiplexer_1_out3), .Q(r3_q), .clk(Clock), .clr(Reset));
  Register #(.width(32)) r4 (.D(WriteD), .en(demultiplexer_1_out4), .Q(r4_q), .clk(Clock), .clr(Reset));
  Register #(.width(32)) r5 (.D(WriteD), .en(demultiplexer_1_out5), .Q(r5_q), .clk(Clock), .clr(Reset));
  Register #(.width(32)) r6 (.D(WriteD), .en(demultiplexer_1_out6), .Q(r6_q), .clk(Clock), .clr(Reset));
  Register #(.width(32)) r7 (.D(WriteD), .en(demultiplexer_1_out7), .Q(r7_q), .clk(Clock), .clr(Reset));
  Register #(.width(32)) r8 (.D(WriteD), .en(demultiplexer_1_out8), .Q(r8_q), .clk(Clock), .clr(Reset));
  Register #(.width(32)) r9 (.D(WriteD), .en(demultiplexer_1_out9), .Q(r9_q), .clk(Clock), .clr(Reset));
  Register #(.width(32)) r10 (.D(WriteD), .en(demultiplexer_1_out10), .Q(r10_q), .clk(Clock), .clr(Reset));
  Register #(.width(32)) r11 (.D(WriteD), .en(demultiplexer_1_out11), .Q(r11_q), .clk(Clock), .clr(Reset));
  Register #(.width(32)) r12 (.D(WriteD), .en(demultiplexer_1_out12), .Q(r12_q), .clk(Clock), .clr(Reset));
  Register #(.width(32)) r13 (.D(WriteD), .en(demultiplexer_1_out13), .Q(r13_q), .clk(Clock), .clr(Reset));
  Register #(.width(32)) r14 (.D(multiplexer_1_out), .en(or_1_out), .Q(r14_q), .clk(or_2_out));  // open: clr
  Register #(.width(32)) r15 (.D(WriteD), .en(demultiplexer_1_out15), .Q(r15_q), .clk(Clock), .clr(Reset));
  Multiplexer #(.select(4), .width(32), .disabled(0), .enable("false")) multiplexer_2 (
    .in0(r0_q), .in1(r1_q), .in2(r2_q), .in3(r3_q), .in4(r4_q), .in5(r5_q), .in6(r6_q), .in7(r7_q),
    .in8(r8_q), .in9(r9_q), .in10(r10_q), .in11(r11_q), .in12(r12_q), .in13(r13_q), .in14(r14_q),
    .in15(r15_q), .out(D1), .sel(Rs1));
  Multiplexer #(.select(4), .width(32), .disabled(0), .enable("false")) multiplexer_3 (
    .in0(r0_q), .in1(r1_q), .in2(r2_q), .in3(r3_q), .in4(r4_q), .in5(r5_q), .in6(r6_q), .in7(r7_q),
    .in8(r8_q), .in9(r9_q), .in10(r10_q), .in11(r11_q), .in12(r12_q), .in13(r13_q), .in14(r14_q),
    .in15(r15_q), .out(D2), .sel(Rs2));
  Multiplexer #(.select(4), .width(32), .disabled(0), .enable("false")) multiplexer_4 (
    .in0(r0_q), .in1(r1_q), .in2(r2_q), .in3(r3_q), .in4(r4_q), .in5(r5_q), .in6(r6_q), .in7(r7_q),
    .in8(r8_q), .in9(r9_q), .in10(r10_q), .in11(r11_q), .in12(r12_q), .in13(r13_q), .in14(r14_q),
    .in15(r15_q), .out({multiplexer_4_out, ShiftAmt}), .sel(Shiftregister));

  // Other names for the same wires on the sheet: Clk = Clock
endmodule

module of (
  input  [31:0] PC,
  input  [31:0] Inst,
  output [31:0] PC_2,
  output [14:0] Cond_Signals,
  output isWb,
  output isBranch,
  output isLd,
  output isSt,
  output isS,
  output [15:0] ALU_Signals,
  output isImm,
  output [3:0] Rd,
  output [31:0] B,
  output [31:0] A,
  output [23:0] Offset
);

  wire [4:0] adder_1_out, register_file_1_shiftamt;
  wire [31:0] multiplexer_1_out, multiplexer_2_out, multiplexer_3_out, register_file_1_d2, shifter_1_out,
       shifter_2_out, shifter_3_out, shifter_4_out, shifter_5_out, shifter_6_out, shifter_7_out,
       shifter_8_out, shifter_9_out;

  Register_File register_file_1 (
    .Rs1(Inst[19:16]), .Rs2(Inst[3:0]), .D1(A), .D2(register_file_1_d2), .ShiftAmt(register_file_1_shiftamt),
    .Shiftregister(Inst[11:8]));  // open: WriteE, WriteD, Clock, Reset, WriteA
  Shifter #(.width(32)) shifter_1 (.in(register_file_1_d2), .\dist (Inst[11:7]), .out(shifter_1_out));
  Shifter #(.width(32), .shift("lr")) shifter_2 (.in(register_file_1_d2), .\dist (Inst[11:7]), .out(shifter_2_out));
  Shifter #(.width(32), .shift("ar")) shifter_3 (.in(register_file_1_d2), .\dist (Inst[11:7]), .out(shifter_3_out));
  Shifter #(.width(32), .shift("rr")) shifter_4 (.in(register_file_1_d2), .\dist (Inst[11:7]), .out(shifter_4_out));
  Shifter #(.width(32)) shifter_5 (.in(register_file_1_d2), .\dist (register_file_1_shiftamt), .out(shifter_5_out));
  Shifter #(.width(32), .shift("lr")) shifter_6 (
    .in(register_file_1_d2), .\dist (register_file_1_shiftamt), .out(shifter_6_out));
  Shifter #(.width(32), .shift("ar")) shifter_7 (
    .in(register_file_1_d2), .\dist (register_file_1_shiftamt), .out(shifter_7_out));
  Shifter #(.width(32), .shift("rr")) shifter_8 (
    .in(register_file_1_d2), .\dist (register_file_1_shiftamt), .out(shifter_8_out));
  Adder #(.width(5)) adder_1 (.a({1'b0, Inst[11:8]}), .b({1'b0, Inst[11:8]}), .out(adder_1_out));  // open: cin, cout
  Multiplexer #(.select(2), .width(32)) multiplexer_1 (
    .in0(shifter_1_out), .in1(shifter_2_out), .in2(shifter_3_out), .in3(shifter_4_out),
    .out(multiplexer_1_out), .sel(Inst[6:5]));  // open: en
  CU cu_1 (
    .Opcode(Inst[24:21]), .Cond(Inst[31:28]), .Cond_Signals(Cond_Signals), .ALU_Signals(ALU_Signals),
    .Type_Code(Inst[27:26]), .ImmBit(Inst[25]), .SBit(Inst[20]), .isImm(isImm), .isBranch(isBranch),
    .isWb(isWb), .IsLd(isLd), .isSt(isSt), .isS(isS));
  Multiplexer #(.select(2), .width(32)) multiplexer_2 (
    .in0(shifter_5_out), .in1(shifter_6_out), .in2(shifter_7_out), .in3(shifter_8_out),
    .out(multiplexer_2_out), .sel(Inst[6:5]));  // open: en
  Shifter #(.width(32), .shift("rr")) shifter_9 (
    .in({{24{1'b0}}, Inst[7:0]}), .\dist (adder_1_out), .out(shifter_9_out));
  Multiplexer #(.width(32), .enable("false")) multiplexer_3 (
    .in0(multiplexer_2_out), .in1(multiplexer_1_out), .out(multiplexer_3_out), .sel(Inst[4]));
  Multiplexer #(.width(32), .enable("false")) multiplexer_4 (
    .in0(multiplexer_3_out), .in1(shifter_9_out), .out(B), .sel(Inst[25]));

  assign Offset = Inst[23:0];
  assign PC_2 = PC;
  assign Rd = Inst[15:12];

  // Notes on the sheet:
  //   Cond.
  //   Type
  //   Opcode
  //   S
  //   Rd
  //   Rs1
  //   Imm
  //   I
  //   shift Imm
  //   shift Type
  //   shiftI
  //   Rs2
  //   shift Reg
  //   immx
endmodule

// Control Unit
module CU (
  input  [1:0] Type_Code,
  input  SBit,
  input  [3:0] Cond,
  input  [3:0] Opcode,
  input  ImmBit,
  output isBranch,
  output isWb,
  output IsLd,
  output [14:0] Cond_Signals,
  output isSt,
  output isS,
  output [15:0] ALU_Signals,
  output isImm
);

  wire decoder_1_out0, decoder_1_out1, or_1_out;

  Decoder #(.select(2)) decoder_1 (
    .out0(decoder_1_out0), .out1(decoder_1_out1), .out2(isBranch), .sel(Type_Code));  // open: out3, en
  Decoder #(.select(4)) decoder_2 (
    .out0(Cond_Signals[0]), .out1(Cond_Signals[1]), .out2(Cond_Signals[2]), .out3(Cond_Signals[3]),
    .out4(Cond_Signals[4]), .out5(Cond_Signals[5]), .out6(Cond_Signals[6]), .out7(Cond_Signals[7]),
    .out8(Cond_Signals[8]), .out9(Cond_Signals[9]), .out10(Cond_Signals[10]), .out11(Cond_Signals[11]),
    .out12(Cond_Signals[12]), .out13(Cond_Signals[13]), .out14(Cond_Signals[14]), .sel(Cond));  // open: out15, en
  Decoder #(.select(4), .enable("false")) decoder_3 (
    .out0(ALU_Signals[0]), .out1(ALU_Signals[1]), .out2(ALU_Signals[2]), .out3(ALU_Signals[3]),
    .out4(ALU_Signals[4]), .out5(ALU_Signals[5]), .out6(ALU_Signals[6]), .out7(ALU_Signals[7]),
    .out8(ALU_Signals[8]), .out9(ALU_Signals[9]), .out10(ALU_Signals[10]), .out11(ALU_Signals[11]),
    .out12(ALU_Signals[12]), .out13(ALU_Signals[13]), .out14(ALU_Signals[14]), .out15(ALU_Signals[15]),
    .sel(Opcode));
  or or_1 (or_1_out, Opcode[2], ~Opcode[3]);  // OR_Gate
  and and_1 (isWb, decoder_1_out0, or_1_out);
  and and_2 (IsLd, decoder_1_out1, SBit);
  and and_3 (isSt, decoder_1_out1, ~SBit);  // AND_Gate
  and and_4 (isS, decoder_1_out0, SBit);

  assign isImm = ImmBit;
endmodule

module Memory_Unit (
  input  in_1,
  input  isSt,
  input  isLd,
  output [31:0] aluResult,
  output [31:0] ldResult,
  output [31:0] Immediate
);

  wire clock_1_out;

  Clock clock_1 (.out(clock_1_out));
  RAM #(.addrWidth(24), .dataWidth(32), .bus("separate")) ram_1 (
    .addr(aluResult[25:2]), .din(Immediate), .data(ldResult), .str(isSt), .clk(clock_1_out), .ld(isLd),
    .clr(in_1));  // open: sel
endmodule

module flags (
  input  is_S,
  input  [15:0] ALU_Signals,
  input  Z,
  input  C,
  input  N,
  output Z_2,
  output C_2,
  output N_2
);

  wire or_1_out;

  or or_1 (or_1_out, is_S, ALU_Signals[8], ALU_Signals[9], ALU_Signals[10], ALU_Signals[11]);
  D_Flip_Flop d_ff_1 (.clk(or_1_out), .D(Z), .Q(Z_2));  // open: Qn, preset, en, reset
  D_Flip_Flop d_ff_2 (.clk(or_1_out), .D(C), .Q(C_2));  // open: Qn, preset, en, reset
  D_Flip_Flop d_ff_3 (.clk(or_1_out), .D(N), .Q(N_2));  // open: Qn, preset, en, reset
endmodule

module ALU (
  input  S,
  input  C,
  input  [31:0] A,
  input  [31:0] B,
  input  [15:0] ALUsignals,
  output C_2,
  output Z,
  output N,
  output [31:0] aluResult
);

  wire adder_1_cout, not_1_out, or_2_out;
  wire [31:0] adder_1_out, adder_2_out, adder_3_out, and_1_out, and_2_out, controlled_buffer_18_out,
       not_2_out, not_3_out, or_1_out, subtractor_1_out, subtractor_2_out, subtractor_3_out,
       subtractor_4_out, subtractor_5_out, xor_1_out;

  not not_1 (not_1_out, C);
  assign not_2_out = ~B;  // NOT_Gate not_2, 32 bits wide
  Adder #(.width(32)) adder_1 (.a(A), .b(B), .out(adder_1_out), .cout(adder_1_cout));  // open: cin
  Subtractor #(.width(32)) subtractor_1 (.a(A), .b(B), .out(subtractor_1_out));  // open: bin, bout
  Subtractor #(.width(32)) subtractor_2 (.a(B), .b(A), .out(subtractor_2_out));  // open: bin, bout
  Adder #(.width(32)) adder_2 (.a(A), .b(B), .out(adder_2_out), .cin(C), .cout(adder_1_cout));
  Subtractor #(.width(32)) subtractor_3 (.a(A), .b(B), .out(subtractor_3_out), .bin(not_1_out));  // open: bout
  Subtractor #(.width(32)) subtractor_4 (.a(B), .b(A), .out(subtractor_4_out), .bin(not_1_out));  // open: bout
  assign and_1_out = A & B;  // AND_Gate and_1, 32 bits wide
  assign or_1_out = A | B;  // OR_Gate or_1, 32 bits wide
  assign xor_1_out = A ^ B;  // XOR_Gate xor_1, 32 bits wide
  assign and_2_out = A & not_2_out;  // AND_Gate and_2, 32 bits wide
  Subtractor #(.width(32)) subtractor_5 (.a(A), .b(B), .out(subtractor_5_out), .bout(adder_1_cout));  // open: bin
  Adder #(.width(32)) adder_3 (.a(A), .b(B), .out(adder_3_out), .cout(adder_1_cout));  // open: cin
  assign not_3_out = ~B;  // NOT_Gate not_3, 32 bits wide
  assign C_2 = S ? adder_1_cout : 1'bz;  // Controlled_Buffer controlled_buffer_1
  assign aluResult = ALUsignals[4] ? adder_1_out : 32'bz;  // Controlled_Buffer controlled_buffer_2
  assign aluResult = ALUsignals[2] ? subtractor_1_out : 32'bz;  // Controlled_Buffer controlled_buffer_3
  assign aluResult = ALUsignals[2] ? subtractor_2_out : 32'bz;  // Controlled_Buffer controlled_buffer_4
  assign aluResult = ALUsignals[5] ? adder_2_out : 32'bz;  // Controlled_Buffer controlled_buffer_5
  assign aluResult = ALUsignals[2] ? subtractor_3_out : 32'bz;  // Controlled_Buffer controlled_buffer_6
  assign aluResult = ALUsignals[2] ? subtractor_4_out : 32'bz;  // Controlled_Buffer controlled_buffer_7
  assign aluResult = ALUsignals[15] ? not_3_out : 32'bz;  // Controlled_Buffer controlled_buffer_8
  assign aluResult = ALUsignals[13] ? B : 32'bz;  // Controlled_Buffer controlled_buffer_9
  assign aluResult = ALUsignals[0] ? and_1_out : 32'bz;  // Controlled_Buffer controlled_buffer_10
  assign aluResult = ALUsignals[8] ? and_1_out : 32'bz;  // Controlled_Buffer controlled_buffer_11
  assign aluResult = ALUsignals[12] ? or_1_out : 32'bz;  // Controlled_Buffer controlled_buffer_12
  assign aluResult = ALUsignals[1] ? xor_1_out : 32'bz;  // Controlled_Buffer controlled_buffer_13
  assign aluResult = ALUsignals[9] ? xor_1_out : 32'bz;  // Controlled_Buffer controlled_buffer_14
  assign aluResult = ALUsignals[14] ? and_2_out : 32'bz;  // Controlled_Buffer controlled_buffer_15
  assign aluResult = ALUsignals[10] ? subtractor_5_out : 32'bz;  // Controlled_Buffer controlled_buffer_16
  assign aluResult = ALUsignals[11] ? adder_3_out : 32'bz;  // Controlled_Buffer controlled_buffer_17
  Controlled_Buffer #(.width(32)) controlled_buffer_18 (.in(aluResult), .out(controlled_buffer_18_out));  // open: en
  not not_4 (Z, or_2_out);
  or or_2 (or_2_out, aluResult[0], aluResult[1], aluResult[2], aluResult[3], aluResult[4], aluResult[5], aluResult[6], aluResult[7], aluResult[8], aluResult[9], aluResult[10], aluResult[11], aluResult[12], aluResult[13], aluResult[14], aluResult[15], aluResult[16], aluResult[17], aluResult[18], aluResult[19], aluResult[20], aluResult[21], aluResult[22], aluResult[23], aluResult[24], aluResult[25], aluResult[26], aluResult[27], aluResult[28], aluResult[29], aluResult[30], aluResult[31]);

  assign N = aluResult[31];

  // Notes on the sheet:
  //   mov
  //   mvn
  //   add
  //   sub
  //   rev sub
  //   add w/ c
  //   sub w/ c
  //   rev sub /w c
  //   AND
  //   OR
  //   XOR
  //   BIC
  //   CMP
  //   CMN
endmodule

module Branch_Unit (
  input  isBranch,
  input  Z,
  input  N,
  input  C,
  input  [14:0] Cond_Signals,
  input  [23:0] Offset,
  output branchTaken,
  output [31:0] branchTarget
);

  wire and_1_out, and_2_out, controlled_buffer_1_out, controlled_buffer_2_out, controlled_buffer_3_out,
       controlled_buffer_4_out, controlled_buffer_5_out, controlled_buffer_6_out, controlled_buffer_7_out,
       controlled_buffer_8_out, controlled_buffer_9_out, controlled_buffer_10_out, controlled_buffer_11_out,
       controlled_buffer_12_out, controlled_buffer_13_out, not_1_out, not_2_out, not_3_out, not_4_out,
       or_1_out, or_2_out, or_3_out;
  wire [31:0] bit_extender_1_out;

  assign bit_extender_1_out = {{8{Offset[23]}}, Offset};  // Bit_Extender bit_extender_1
  not not_1 (not_1_out, Z);
  not not_2 (not_2_out, N);
  not not_3 (not_3_out, C);
  not not_4 (not_4_out, N);
  and and_1 (and_1_out, ~Z, C);  // AND_Gate
  or or_1 (or_1_out, ~C, Z);  // OR_Gate
  and and_2 (and_2_out, ~Z, ~N);  // AND_Gate
  or or_2 (or_2_out, N, Z);
  Shifter #(.width(32)) shifter_1 (.in(bit_extender_1_out), .\dist (5'b00010), .out(branchTarget));
  assign controlled_buffer_1_out = Cond_Signals[0] ? Z : 1'bz;  // Controlled_Buffer controlled_buffer_1
  assign controlled_buffer_2_out = Cond_Signals[1] ? not_1_out : 1'bz;  // Controlled_Buffer controlled_buffer_2
  assign controlled_buffer_3_out = Cond_Signals[4] ? N : 1'bz;  // Controlled_Buffer controlled_buffer_3
  assign controlled_buffer_4_out = Cond_Signals[5] ? not_2_out : 1'bz;  // Controlled_Buffer controlled_buffer_4
  assign controlled_buffer_5_out = Cond_Signals[2] ? C : 1'bz;  // Controlled_Buffer controlled_buffer_5
  assign controlled_buffer_6_out = Cond_Signals[3] ? not_3_out : 1'bz;  // Controlled_Buffer controlled_buffer_6
  assign controlled_buffer_7_out = Cond_Signals[8] ? and_1_out : 1'bz;  // Controlled_Buffer controlled_buffer_7
  assign controlled_buffer_8_out = Cond_Signals[9] ? or_1_out : 1'bz;  // Controlled_Buffer controlled_buffer_8
  assign controlled_buffer_9_out = Cond_Signals[11] ? N : 1'bz;  // Controlled_Buffer controlled_buffer_9
  assign controlled_buffer_10_out = Cond_Signals[10] ? not_4_out : 1'bz;  // Controlled_Buffer controlled_buffer_10
  assign controlled_buffer_11_out = Cond_Signals[12] ? and_2_out : 1'bz;  // Controlled_Buffer controlled_buffer_11
  assign controlled_buffer_12_out = Cond_Signals[12] ? or_2_out : 1'bz;  // Controlled_Buffer controlled_buffer_12
  assign controlled_buffer_13_out = Cond_Signals[14] ? 1'b1 : 1'bz;  // Controlled_Buffer controlled_buffer_13
  or or_3 (or_3_out, controlled_buffer_1_out, controlled_buffer_2_out, controlled_buffer_3_out, controlled_buffer_4_out, controlled_buffer_5_out, controlled_buffer_6_out, controlled_buffer_7_out, controlled_buffer_8_out, controlled_buffer_9_out, controlled_buffer_10_out, controlled_buffer_11_out, controlled_buffer_12_out, controlled_buffer_13_out);
  and and_3 (branchTaken, isBranch, or_3_out);
endmodule

module EX (
  input  [31:0] PC,
  input  [31:0] PC_out,
  input  isBranch,
  input  isS,
  input  [15:0] ALU_Signals,
  input  [31:0] A,
  input  [31:0] B,
  input  [14:0] CondSignals,
  input  [23:0] Offset,
  output branchTaken,
  output [31:0] branchTarget,
  output [31:0] aluResult
);

  wire alu_1_c_2, alu_1_n, alu_1_z, Flags_c_2, Flags_n_2, Flags_z_2;

  ALU alu_1 (
    .A(A), .B(B), .ALUsignals(ALU_Signals), .aluResult(aluResult), .C(Flags_c_2), .S(isS), .Z(alu_1_z),
    .N(alu_1_n), .C_2(alu_1_c_2));
  flags Flags (
    .is_S(isS), .ALU_Signals(ALU_Signals), .Z(alu_1_z), .C(alu_1_c_2), .N(alu_1_n), .Z_2(Flags_z_2),
    .C_2(Flags_c_2), .N_2(Flags_n_2));
  Branch_Unit Branch_Unit (
    .isBranch(isBranch), .Z(Flags_z_2), .N(Flags_n_2), .C(Flags_c_2), .Cond_Signals(CondSignals),
    .Offset(Offset), .branchTaken(branchTaken), .branchTarget(branchTarget));

  assign PC_out = PC;
endmodule

module _2bit_Branch_Predictor (
  input  [2:0] _27_25,
  input  [31:0] Pc,
  input  [31:0] TargetAddress,
  input  in_4,
  input  [31:0] Offset_B,
  output branchPrediction
);

  wire and_1_out, and_2_out, and_3_out, d_ff_1_q, d_ff_2_q, d_ff_4_q, decoder_1_out5, or_1_out;
  wire [31:0] adder_1_out, adder_2_out, multiplexer_1_out;

  Decoder #(.select(3), .enable("false")) decoder_1 (
    .out5(decoder_1_out5), .sel(_27_25));  // open: out0, out1, out2, out3, out4, out6, out7
  D_Flip_Flop #(.trigger("falling")) d_ff_1 (
    .clk(decoder_1_out5), .D(in_4), .Q(d_ff_1_q));  // open: Qn, preset, en, reset
  D_Flip_Flop d_ff_2 (.clk(decoder_1_out5), .D(d_ff_1_q), .Q(d_ff_2_q));  // open: Qn, preset, en, reset
  and and_1 (and_1_out, branchPrediction, d_ff_2_q);
  and and_2 (and_2_out, d_ff_4_q, d_ff_2_q);
  and and_3 (and_3_out, branchPrediction, d_ff_4_q);
  Adder #(.width(32)) adder_1 (.a(Pc), .b(32'h4), .out(adder_1_out));  // open: cin, cout
  Adder #(.width(32)) adder_2 (.a(Pc), .b(Offset_B), .out(adder_2_out));  // open: cin, cout
  or or_1 (or_1_out, and_1_out, and_2_out, and_3_out);
  Multiplexer #(.width(32)) multiplexer_1 (
    .in0(adder_1_out), .in1(adder_2_out), .out(multiplexer_1_out), .en(branchPrediction));  // open: sel
  D_Flip_Flop d_ff_3 (.D(or_1_out), .Q(branchPrediction));  // open: clk, Qn, preset, en, reset
  D_Flip_Flop d_ff_4 (.D(d_ff_2_q), .Q(d_ff_4_q));  // open: clk, Qn, preset, en, reset

  // Notes on the sheet:
  //   isBranchTaken
endmodule

module Processor (
);

  wire ex_1_branchtaken, of_ex_1_isbranch_2, OF_isbranch, OF_isimm, OF_isld, OF_iss, OF_isst, OF_iswb,
       undriven, undriven_2;
  wire [3:0] OF_rd;
  wire [14:0] OF_cond_signals, of_ex_1_cond_signals_2;
  wire [15:0] OF_alu_signals, of_ex_1_alu_signals_2;
  wire [23:0] of_ex_1_offset_2, OF_offset;
  wire [31:0] ex_1_aluresult, ex_1_branchtarget, IF_instruction, IF_OF_inst_out, IF_OF_pc_out, IF_pc, OF_a,
       OF_b, of_ex_1_a_2, of_ex_1_b_2, of_ex_1_pc_out, OF_pc_2, undriven_3;

  main IF (
    .isBranchTaken(ex_1_branchtaken), .branchPC(ex_1_branchtarget), .PC(IF_pc), .Instruction(IF_instruction),
    .Reset(undriven));
  IF_OF IF_OF (
    .PC(IF_pc), .instruction(IF_instruction), .isStall(undriven_2), .PC_out(IF_OF_pc_out),
    .inst_out(IF_OF_inst_out));
  of OF (
    .PC(IF_OF_pc_out), .Inst(IF_OF_inst_out), .PC_2(OF_pc_2), .Cond_Signals(OF_cond_signals),
    .ALU_Signals(OF_alu_signals), .isImm(OF_isimm), .Rd(OF_rd), .B(OF_b), .A(OF_a), .isBranch(OF_isbranch),
    .isWb(OF_iswb), .isLd(OF_isld), .isSt(OF_isst), .isS(OF_iss), .Offset(OF_offset));
  OF_EX of_ex_1 (
    .PC(OF_pc_2), .Cond_Signals(OF_cond_signals), .isBranch(OF_isbranch), .ALU_Signals(OF_alu_signals),
    .isImm(OF_isimm), .isS(OF_iss), .Rd(OF_rd), .A(OF_a), .B(OF_b), .PC_out(of_ex_1_pc_out),
    .Cond_Signals_2(of_ex_1_cond_signals_2), .isBranch_2(of_ex_1_isbranch_2),
    .ALU_Signals_2(of_ex_1_alu_signals_2), .isS_2(of_ex_1_isbranch_2), .A_2(of_ex_1_a_2), .B_2(of_ex_1_b_2),
    .is_Stall(undriven_2), .isWb(OF_iswb), .isLd(OF_isld), .isSt(OF_isst), .Offset(OF_offset),
    .Offset_2(of_ex_1_offset_2));  // open: isImm_2, Rd_2, isWB_2, isLd_2, isSt_2
  EX ex_1 (
    .PC(of_ex_1_pc_out), .isBranch(of_ex_1_isbranch_2), .isS(of_ex_1_isbranch_2),
    .ALU_Signals(of_ex_1_alu_signals_2), .A(of_ex_1_a_2), .B(of_ex_1_b_2),
    .CondSignals(of_ex_1_cond_signals_2), .Offset(of_ex_1_offset_2), .PC_out(undriven_3),
    .branchTaken(ex_1_branchtaken), .branchTarget(ex_1_branchtarget), .aluResult(ex_1_aluresult));
endmodule

module IF_OF (
  input  [31:0] PC,
  input  [31:0] instruction,
  input  isStall,
  output [31:0] PC_out,
  output [31:0] inst_out
);

  wire and_1_out, not_1_out, undriven;

  Clock clock_1 ();  // open: out
  not not_1 (not_1_out, isStall);
  and and_1 (and_1_out, undriven, not_1_out);
  Register #(.width(32)) register_1 (.D(PC), .Q(PC_out), .clk(and_1_out));  // open: en, clr
  Register #(.width(32)) register_2 (.D(instruction), .Q(inst_out), .clk(and_1_out));  // open: en, clr
endmodule

module OF_EX (
  input  [31:0] PC,
  input  [14:0] Cond_Signals,
  input  isBranch,
  input  isWb,
  input  isLd,
  input  isSt,
  input  [15:0] ALU_Signals,
  input  isImm,
  input  isS,
  input  [3:0] Rd,
  input  [31:0] A,
  input  [31:0] B,
  input  [23:0] Offset,
  input  is_Stall,
  output [31:0] PC_out,
  output [14:0] Cond_Signals_2,
  output isBranch_2,
  output isWB_2,
  output isLd_2,
  output isSt_2,
  output [15:0] ALU_Signals_2,
  output isImm_2,
  output isS_2,
  output [3:0] Rd_2,
  output [31:0] A_2,
  output [31:0] B_2,
  output [23:0] Offset_2
);

  wire and_1_out, clock_1_out, not_1_out;

  Clock clock_1 (.out(clock_1_out));
  not not_1 (not_1_out, is_Stall);
  and and_1 (and_1_out, clock_1_out, not_1_out);
  Register #(.width(32)) register_1 (.D(PC), .Q(PC_out), .clk(and_1_out));  // open: en, clr
  Register #(.width(15)) register_2 (.D(Cond_Signals), .Q(Cond_Signals_2), .clk(and_1_out));  // open: en, clr
  Register #(.width(1)) register_3 (.D(isBranch), .Q(isBranch_2), .clk(and_1_out));  // open: en, clr
  Register #(.width(1)) register_4 (.D(isWb), .Q(isWB_2), .clk(and_1_out));  // open: en, clr
  Register #(.width(1)) register_5 (.D(isLd), .Q(isLd_2), .clk(and_1_out));  // open: en, clr
  Register #(.width(1)) register_6 (.D(isSt), .Q(isSt_2), .clk(and_1_out));  // open: en, clr
  Register #(.width(16)) register_7 (.D(ALU_Signals), .Q(ALU_Signals_2), .clk(and_1_out));  // open: en, clr
  Register #(.width(1)) register_8 (.D(isImm), .Q(isImm_2), .clk(and_1_out));  // open: en, clr
  Register #(.width(1)) register_9 (.D(isS), .Q(isS_2), .clk(and_1_out));  // open: en, clr
  Register #(.width(4)) register_10 (.D(Rd), .Q(Rd_2), .clk(and_1_out));  // open: en, clr
  Register #(.width(32)) register_11 (.D(A), .Q(A_2), .clk(and_1_out));  // open: en, clr
  Register #(.width(32)) register_12 (.D(B), .Q(B_2), .clk(and_1_out));  // open: en, clr
  Register #(.width(24)) register_13 (.D(Offset), .Q(Offset_2), .clk(and_1_out));  // open: en, clr
endmodule
