// Logisim project IF.circ as structural Verilog: 4 circuits, main circuit main
module main (
  input  isBranchTaken,
  input  [31:0] in_2,
  input  in_3,
  output [31:0] out_4
);

  wire Clk_out;
  wire [31:0] adder_1_out, multiplexer_1_out, PC_q;

  Register #(.width(32), .trigger("falling")) PC (
    .D(multiplexer_1_out), .en(1'b1), .Q(PC_q), .clk(Clk_out), .clr(in_3));
  Clock Clk (.out(Clk_out));
  Adder #(.width(32)) adder_1 (.a(32'h4), .b(PC_q), .out(adder_1_out));  // open: cin, cout
  ROM #(.addrWidth(24), .dataWidth(32)) rom_1 (.addr(PC_q[25:2]), .data(out_4));  // open: sel
  Multiplexer #(.width(32), .enable("false")) multiplexer_1 (
    .in0(adder_1_out), .in1(in_2), .out(multiplexer_1_out), .sel(isBranchTaken));
  Memory_Unit memory_unit_1 ();  // open: aluResult, Immediate, isSt, isLd, Reset, ldResult

  // Notes on the sheet:
  //   contents of rom_1 (hex, n*v repeats v):
  //   54400003 54400024
  //   Instruction
  //   branchPC
endmodule

module of (
  input  [31:0] PC,
  input  [31:0] Inst,
  output [15:0] ALU_Signals,
  output [31:0] out_4,
  output [31:0] out_5,
  output [31:0] out_6
);

  wire [4:0] adder_1_out, undriven;
  wire [31:0] multiplexer_1_out, multiplexer_2_out, shifter_1_out, shifter_2_out, shifter_3_out,
       shifter_4_out, shifter_5_out, shifter_6_out, shifter_7_out, shifter_8_out, undriven_2;

  Shifter #(.width(32)) shifter_1 (.in(undriven_2), .\dist (Inst[11:7]), .out(shifter_1_out));
  Shifter #(.width(32), .shift("lr")) shifter_2 (.in(undriven_2), .\dist (Inst[11:7]), .out(shifter_2_out));
  Shifter #(.width(32), .shift("ar")) shifter_3 (.in(undriven_2), .\dist (Inst[11:7]), .out(shifter_3_out));
  Shifter #(.width(32), .shift("rr")) shifter_4 (.in(undriven_2), .\dist (Inst[11:7]), .out(shifter_4_out));
  Shifter #(.width(32)) shifter_5 (.in(undriven_2), .\dist (undriven), .out(shifter_5_out));
  Shifter #(.width(32), .shift("lr")) shifter_6 (.in(undriven_2), .\dist (undriven), .out(shifter_6_out));
  Shifter #(.width(32), .shift("ar")) shifter_7 (.in(undriven_2), .\dist (undriven), .out(shifter_7_out));
  Shifter #(.width(32), .shift("rr")) shifter_8 (.in(undriven_2), .\dist (undriven), .out(shifter_8_out));
  CU cu_1 (
    .opcode(Inst[24:21]), .isAND(ALU_Signals[0]), .isEOR(ALU_Signals[1]), .isSUB(ALU_Signals[2]),
    .isRSB(ALU_Signals[3]), .isADD(ALU_Signals[4]), .isADC(ALU_Signals[5]), .isSBC(ALU_Signals[6]),
    .isRSC(ALU_Signals[7]), .isTST(ALU_Signals[8]), .isTEQ(ALU_Signals[9]), .isCMP(ALU_Signals[10]),
    .isCMN(ALU_Signals[11]), .isORR(ALU_Signals[12]), .isMOV(ALU_Signals[13]), .isBIC(ALU_Signals[14]),
    .isMVN(ALU_Signals[15]));
  Adder #(.width(5)) adder_1 (.a({1'b0, Inst[11:8]}), .b({1'b0, Inst[11:8]}), .out(adder_1_out));  // open: cin, cout
  Multiplexer #(.select(2), .width(32)) multiplexer_1 (
    .in0(shifter_1_out), .in1(shifter_2_out), .in2(shifter_3_out), .in3(shifter_4_out),
    .out(multiplexer_1_out), .sel(Inst[6:5]));  // open: en
  Multiplexer #(.select(2), .width(32)) multiplexer_2 (
    .in0(shifter_5_out), .in1(shifter_6_out), .in2(shifter_7_out), .in3(shifter_8_out),
    .out(multiplexer_2_out), .sel(Inst[6:5]));  // open: en
  Shifter #(.width(32), .shift("rr")) shifter_9 (.in({{24{1'b0}}, Inst[7:0]}), .\dist (adder_1_out), .out(out_4));
  Multiplexer #(.width(32), .enable("false")) multiplexer_3 (
    .in0(multiplexer_2_out), .in1(multiplexer_1_out), .out(out_6), .sel(Inst[4]));
  Multiplexer #(.width(32), .enable("false")) multiplexer_4 (.in0(out_6), .in1(out_4), .out(out_5), .sel(Inst[25]));

  // Notes on the sheet:
  //   Cond.
  //   Type
  //   Opcode
  //   S
  //   Rd
  //   Imm
  //   shift Type
  //   shiftI
  //   Read ShiftReg
  //   Rs2
  //   Rs1
  //   REG FILE
endmodule

// Control Unit
module CU (
  input  [3:0] opcode,
  output isAND,
  output isEOR,
  output isSUB,
  output isRSB,
  output isADD,
  output isADC,
  output isSBC,
  output isRSC,
  output isTST,
  output isTEQ,
  output isCMP,
  output isCMN,
  output isORR,
  output isMOV,
  output isBIC,
  output isMVN
);

  Decoder #(.select(4), .enable("false")) decoder_1 (
    .out0(isAND), .out1(isEOR), .out2(isSUB), .out3(isRSB), .out4(isADD), .out5(isADC), .out6(isSBC),
    .out7(isRSC), .out8(isTST), .out9(isTEQ), .out10(isCMP), .out11(isCMN), .out12(isORR), .out13(isMOV),
    .out14(isBIC), .out15(isMVN), .sel(opcode));
endmodule

module Memory_Unit (
  input  isSt,
  input  isLd,
  input  Reset,
  output [23:0] aluResult,
  output [31:0] ldResult,
  output [31:0] Immediate
);

  wire clock_1_out, undriven, undriven_2, undriven_3;

  Clock clock_1 (.out(clock_1_out));
  RAM #(.addrWidth(24), .dataWidth(32), .bus("separate")) ram_1 (
    .addr(aluResult), .din(Immediate), .data(ldResult), .str(undriven), .clk(clock_1_out), .ld(undriven_2),
    .clr(undriven_3));  // open: sel
endmodule
