// Logisim project cache.circ as structural Verilog: 1 circuit, main circuit cacheMemory
module cacheMemory (
  input  [31:0] address,
  input  [31:0] cacheL0,
  input  [31:0] cacheL1,
  input  [31:0] cacheL2,
  input  [31:0] cacheL3,
  input  [31:0] cacheL4,
  input  [31:0] cacheL5,
  input  [31:0] cacheL6,
  input  [31:0] cacheL7
);

  wire and_1_out, comparator_1_eq, multiplexer_2_out;
  wire [3:0] multiplexer_3_out, multiplexer_4_out;
  wire [26:0] multiplexer_1_out;

  Multiplexer #(.select(3), .width(27)) multiplexer_1 (
    .in0(cacheL0[30:4]), .in1(cacheL1[30:4]), .in2(cacheL2[30:4]), .in3(cacheL3[30:4]), .in4(cacheL4[30:4]),
    .in5(cacheL5[30:4]), .in6(cacheL6[30:4]), .in7(cacheL7[30:4]), .out(multiplexer_1_out), .sel(address[4:2]));  // open: en
  Multiplexer #(.select(3)) multiplexer_2 (
    .in0(cacheL0[31]), .in1(cacheL1[31]), .in2(cacheL2[31]), .in3(cacheL3[31]), .in4(cacheL4[31]),
    .in5(cacheL5[31]), .in6(cacheL6[31]), .in7(cacheL7[31]), .out(multiplexer_2_out), .sel(address[4:2]));  // open: en
  Comparator #(.width(27)) comparator_1 (
    .a(multiplexer_1_out), .b(address[31:5]), .eq(comparator_1_eq));  // open: gt, lt
  Multiplexer #(.select(3), .width(4)) multiplexer_3 (
    .in0(cacheL0[3:0]), .in1(cacheL1[3:0]), .in2(cacheL2[3:0]), .in3(cacheL3[3:0]), .in4(cacheL4[3:0]),
    .in5(cacheL5[3:0]), .in6(cacheL6[3:0]), .in7(cacheL7[3:0]), .out(multiplexer_3_out), .sel(address[4:2]));  // open: en
  and and_1 (and_1_out, comparator_1_eq, multiplexer_2_out);
  Multiplexer #(.width(4)) multiplexer_4 (
    .in1(multiplexer_3_out), .out(multiplexer_4_out), .sel(and_1_out));  // open: in0, en
  // Probe on and_1_out
  // Probe on multiplexer_4_out

  // Notes on the sheet:
  //   Cache Memory
  //   data
  //   block#
  //   valid
  //   line# of cache
  //   block#
  //   Block number equal?
  //   Validity in cache?
  //   Data
  //   Cache hit
endmodule
